# Fritzing sketch circuit (saved by Fritzing 0.7.12b)
breadboards: 2

parts:
  Arduino_Ethernet_Shield1 = Arduino Ethernet Shield
  10k = Resistor [tolerance=±5% resistance=10k package=THT]
  temp_sensor = LM35 Temperature Sensor [package="TO92 [THT]"]
  photo-resistor = Photocell (LDR) [package=THT]
  10k_2 = Resistor [tolerance=±5% resistance=10k package=THT]
  12V_Barrel_connector = Power plug
  Pump_relay = Relay [part_number=FRS1B-S package=THT]
  330 = Resistor [tolerance=±5% resistance=330 package=THT]
  D1 = Rectifier Diode [part_number=1N4001 package="300 mil [THT]"]
  D2 = Rectifier Diode [part_number=1N4001 package="300 mil [THT]"]
  12V_350GPH_bilge_pump = DC Motor
  Q1 = NPN-Transistor [package="TO92 [THT]"]
  Galvanized_nail = Antenna
  Galvanized_Nail = Antenna

nets:
  N1: Arduino_Ethernet_Shield1.D5, 330.Pin_1
  N2: Arduino_Ethernet_Shield1.D3, 10k.Pin_0
  N3: Arduino_Ethernet_Shield1.+5V, temp_sensor.+Vs, 10k_2.Pin_1, Pump_relay.COIL1, D1.cathode
  GND: Arduino_Ethernet_Shield1.GND, temp_sensor.GND, photo-resistor.pin_0, Q1.C, Galvanized_nail.antenna_lead
  N4: Arduino_Ethernet_Shield1.A0, temp_sensor.Vout
  N5: Arduino_Ethernet_Shield1.A1, photo-resistor.pin_1, 10k_2.Pin_0
  N6: Arduino_Ethernet_Shield1.A2, 10k.Pin_1, Galvanized_Nail.antenna_lead
  N7: 12V_Barrel_connector.VCC, Pump_relay.B
  N8: 12V_Barrel_connector.GND, D2.anode, 12V_350GPH_bilge_pump.pin_2
  N9: Pump_relay.C1, Pump_relay.C2, D2.cathode, 12V_350GPH_bilge_pump.pin_1
  N10: Pump_relay.COIL2, D1.anode, Q1.E
  N11: 330.Pin_0, Q1.B
